// Digital circuit ASSERT.dig as structural Verilog
// This cricuit provide assert function. you can write value to 
// special address to excute assert function.
//  0xFF: value0,
//  0xFE: value1,
//  0xFD: function select(
//   0: break
//   1: assert v0 > v1, 
//   2: assert v0 = v1, 
//   3: assert v0 < v1)
// If assert  failed(F is high) when CLK falling edge, CLKO will ouput low.
module ASSERT (
  input  C,
  input  [7:0] D,
  input  [7:0] A,
  input  WE,
  output F
);

  wire and_1_out, and_2_out, and_3_out, comparator_1_eq, comparator_2_eq, comparator_3_eq, comparator_4_eq,
       comparator_4_gt, comparator_4_lt, multiplexer_1_out, not_1_out, not_2_out, not_3_out;
  wire [7:0] PAR0_q, PAR1_q;

  Comparator #(.Bits(8)) comparator_1 (.a(A), .b({8{1'b1}}), .eq(comparator_1_eq));  // open: gt, lt
  Comparator #(.Bits(8)) comparator_2 (.a(A), .b(8'hfe), .eq(comparator_2_eq));  // open: gt, lt
  Comparator #(.Bits(8)) comparator_3 (.a(A), .b(8'hfd), .eq(comparator_3_eq));  // open: gt, lt
  and and_1 (and_1_out, comparator_1_eq, WE);
  and and_2 (and_2_out, comparator_2_eq, WE);
  and and_3 (and_3_out, comparator_3_eq, WE);
  Register #(.Bits(8)) PAR0 (.D(D), .C(C), .en(and_1_out), .Q(PAR0_q));
  Register #(.Bits(8)) PAR1 (.D(D), .C(C), .en(and_2_out), .Q(PAR1_q));
  Comparator #(.Bits(8)) comparator_4 (
    .a(PAR0_q), .b(PAR1_q), .gt(comparator_4_gt), .eq(comparator_4_eq), .lt(comparator_4_lt));
  not not_1 (not_1_out, comparator_4_gt);
  not not_2 (not_2_out, comparator_4_eq);
  not not_3 (not_3_out, comparator_4_lt);
  Multiplexer #(.Selector_Bits(2)) multiplexer_1 (
    .sel(D[1:0]), .in_0(1'b1), .in_1(not_1_out), .in_2(not_2_out), .in_3(not_3_out), .out(multiplexer_1_out));
  and and_4 (F, multiplexer_1_out, and_3_out);

  // Notes on the sheet:
  //   C: Clock
  //   D: Data in
  //   A: Address to locate register
  //   WE: Write enable
  //   F: Assert false flag.
  //   CLKO will be disabled at next cycle if it's high.
endmodule
