// Digital circuit BR.dig as structural Verilog
module BR (
  input  C,
  input  R,
  input  [2:0] S,
  input  ALUDF,
  input  ALUSF,
  input  A0,
  input  A7,
  output Q
);

  wire d_ff_1_nq, multiplexer_1_out, multiplexer_2_out;

  Multiplexer #(.Selector_Bits(3)) multiplexer_1 (
    .sel(S), .in_0(Q), .in_1(d_ff_1_nq), .in_2(1'b0), .in_3(1'b1), .in_4(ALUSF), .in_5(ALUDF), .in_6(A7),
    .in_7(A0), .out(multiplexer_1_out));
  Multiplexer multiplexer_2 (.sel(R), .in_0(multiplexer_1_out), .in_1(1'b0), .out(multiplexer_2_out));
  D_FF d_ff_1 (.D(multiplexer_2_out), .C(C), .Q(Q), .nQ(d_ff_1_nq));

  // Notes on the sheet:
  //   C: Clock
  //   R: Sync clear
endmodule
