// Digital circuit DCOUTER.dig as structural Verilog
module DCOUTER (
  input  CLK,
  input  nCLR,
  input  CNT,
  input  nLE,
  input  [11:0] D,
  output [11:0] Q
);

  wire not_1_out, not_2_out, or_1_out;
  wire [11:0] add_1_s, reg__sync_clear_1_p1;

  not not_1 (not_1_out, nLE);
  not not_2 (not_2_out, nCLR);
  or or_1 (or_1_out, CNT, not_1_out);
  // reg__sync_clear #(.generic("Bits := args.Bits;")) reg__sync_clear_1: pin names not known; wires that end beside it: reg__sync_clear_1_p1, CLK, not_2_out, or_1_out, Q
  Add #(.Bits(12), .generic("Bits := int(args.Bits);")) add_1 (.a(12'h1), .b(Q), .c_i(1'b0), .s(add_1_s));  // open: c_o
  Multiplexer #(.Bits(12), .generic("Bits := int(args.Bits);")) multiplexer_1 (
    .sel(not_1_out), .in_0(add_1_s), .in_1(D), .out(reg__sync_clear_1_p1));

  // Notes on the sheet:
  //   CNT: Q = Q + 1, lower priority than LE
  //   nLE: load value from D
endmodule
