// Digital circuit EXTCTL.dig as structural Verilog
// The circuit was using to make condition exit in Java
// (see Digitalc.exe's source code, MainCmd.java). 
// When you write a value greater than 0 to EXR (0xFC),
// The debug simulator will consider the program to end normally.
module EXTCTL (
  input  WE,
  input  [7:0] A,
  input  [7:0] D,
  input  C,
  output [7:0] V0
);

  wire and_1_out, comparator_1_eq;

  Comparator #(.Bits(8)) comparator_1 (.a(A), .b(8'hfc), .eq(comparator_1_eq));  // open: gt, lt
  and and_1 (and_1_out, comparator_1_eq, WE);
  Register #(.Bits(8)) EXR (.D(D), .C(C), .en(and_1_out), .Q(V0));
  // Pins of 1 and 8 bits meet at D
  // Pins of 1 and 8 bits meet at V0
  // Pins of 1 and 8 bits meet at A

  // Notes on the sheet:
  //   WE: write enable
  //   A: Address
  //   D: Data
  //   C: CLK
  //   V0: EXR value
endmodule
