// Digital circuit INT.dig as structural Verilog
// PC external, for debug purpose, laod PC from RF to this register.
// select byte PCEL when RS is 8, select byte PCEH when RS is 9.
module INT (
  input  CLK,
  input  CLR,
  input  [7:0] A,
  input  [7:0] D,
  input  WE,
  input  OE,
  input  nIRQ_OE,
  input  CAI,
  input  RI,
  input  TI,
  output [7:0] IRQ
);

  wire and_1_out, comparator_1_eq, nand_1_out;
  wire [7:0] int_tcon_1_q;

  Comparator #(.Bits(8)) comparator_1 (.a(A), .b(8'h88), .eq(comparator_1_eq));  // open: gt, lt
  nand nand_1 (nand_1_out, WE, comparator_1_eq);
  and and_1 (and_1_out, comparator_1_eq, OE);
  INT_TCON int_tcon_1 (.D(D), .WE(nand_1_out), .CII(CAI), .CLK(CLK), .CLR(CLR), .IRQ(IRQ[3:0]), .Q(int_tcon_1_q));
  SCON SCON (.CLK(CLK), .CLR(CLR), .IO(D), .A(A), .OE(OE), .WE(WE), .RI(RI), .TI(TI), .TRI(IRQ[4]));
  assign D = and_1_out ? int_tcon_1_q : 8'bz;  // Driver driver_1
  assign D = ~nIRQ_OE ? {3'b000, IRQ[4:0]} : 8'bz;  // DriverInvSel driverinvsel_1

  assign IRQ[7:5] = 3'b000;

  // Notes on the sheet:
  //   CAI: clear accepted interrupt
endmodule
