// Digital circuit RAM.dig as structural Verilog
// stop ouput clock if input S  is high. if go is 1, clock will ouput normally.
module RAM (
  input  CLK,
  input  [7:0] A,
  input  WE,
  input  OE,
  input  Dt,
  output [7:0] O
);

  wire and_1_out, and_2_out, not_1_out;

  and and_1 (and_1_out, A[7], Dt);
  and and_2 (and_2_out, WE, CLK, not_1_out);
  not not_1 (not_1_out, CLK);
  RAMSinglePortSel #(.AddrBits(8), .isProgramMemory("true"), .Bits(8)) RAM (
    .A(A), .CS(~and_1_out), .WE(and_2_out), .OE(OE), .D(O));

  // Notes on the sheet:
  //   A: address
  //   Dt: Direct address mode flag, it's will disable RAM when address is in
  //   0x80-0xFF.
endmodule
