// Digital circuit ROM.dig as structural Verilog
module ROM (
  input  [15:0] A,
  input  nOE,
  input  [7:0] IMMED,
  input  CLK,
  input  nPRRWE,
  input  [7:0] D
);

  wire and_2_out, and_3_out, and_4_out, nA_B, nand_1_out, nBUFCE, nCE, nWE, or_1_out, or_2_out, reset_1_out;
  wire [2:2] PRR_q;
  wire [7:0] ROM_d;

  Register #(.Bits(3)) PRR (.D(IMMED[2:0]), .C(CLK), .en(~nPRRWE), .Q({PRR_q[2], nCE, nA_B}));
  nand nand_1 (nand_1_out, nA_B, nA_B);
  Reset reset_1 (.out(reset_1_out));
  and and_1 (nBUFCE, nOE, nand_1_out);
  xor xor_1 (nWE, PRR_q[2], 1'b1);
  and and_2 (and_2_out, ~nCE, reset_1_out);  // And
  and and_3 (and_3_out, ~nWE, reset_1_out);  // And
  and and_4 (and_4_out, ~nA_B, reset_1_out);  // And
  EEPROM #(.AddrBits(16), .isProgramMemory("true"), .Bits(8)) ROM (
    .A(A), .CS(and_2_out), .WE(and_3_out), .OE(and_4_out), .D(ROM_d));
  or or_1 (or_1_out, nBUFCE, ~nA_B);  // Or
  or or_2 (or_2_out, nBUFCE, nA_B);
  assign D = ~or_2_out ? ROM_d : 8'bz;  // DriverInvSel driverinvsel_1
  assign ROM_d = ~or_1_out ? D : 8'bz;  // DriverInvSel driverinvsel_2

  // Notes on the sheet:
  //   A: address
  //   nOE: default 1
  //   nPRRWE: default 1
  //   it's necessary to prevent accidental writing to ROM
  //   contents of ROM (hex, n*v repeats v):
  //   70,0,75,0,ff,76,0,75,0,fe,76,0,75,0,fd,76,0,75,0,fc,76,0,75,0,fb,76,0,75,0,fa,76,
  //   0,75,0,f9,76,0,75,0,f8,76,0,75,0,f7,76,0,75,0,f6,76,0,75,0,f5,76,0,75,0,f4,76,0,75,
  //   0,f3,76,0,75,0,f2,76,0,75,0,f1,76,0,75,0,f0,76,0,75,0,ef,76,0,75,0,ee,76,0,75,0,ed,
  //   76,0,75,0,ec,76,0,75,0,eb,76,0,75,0,ea,76,0,75,0,e9,76,0,75,0,e8,76,0,75,0,e7,76,
  //   0,75,0,e6,76,0,75,0,e5,76,0,75,0,e4,76,0,75,0,e3,76,0,75,0,e2,76,0,75,0,e1,76,0,75,
  //   0,e0,76,0,75,0,df,76,0,75,0,de,76,0,75,0,dd,76,0,75,0,dc,76,0,75,0,db,76,0,75,0,da,
  //   76,0,75,0,d9,76,0,75,0,d8,76,0,75,0,d7,76,0,75,0,d6,76,0,75,0,d5,76,0,75,0,d4,76,
  //   0,75,0,d3,76,0,75,0,d2,76,0,75,0,d1,76,0,75,0,d0,76,0,75,0,cf,76,0,75,0,ce,76,0,75,
  //   0,cd,76,0,75,0,cc,76,0,75,0,cb,76,0,75,0,ca,76,0,75,0,c9,76,0,75,0,c8,76,0,75,0,c7,
  //   76,0,75,0,c6,76,0,75,0,c5,76,0,75,0,c4,76,0,75,0,c3,76,0,75,0,c2,76,0,75,0,c1,76,
  //   0,75,0,c0,76,0,75,0,bf,76,0,75,0,be,76,0,75,0,bd,76,0,75,0,bc,76,0,75,0,bb,76,0,75,
  //   0,ba,76,0,75,0,b9,76,0,75,0,b8,76,0,75,0,b7,76,0,75,0,b6,76,0,75,0,b5,76,0,75,0,b4,
  //   76,0,75,0,b3,76,0,75,0,b2,76,0,75,0,b1,76,0,75,0,b0,76,0,75,0,af,76,0,75,0,ae,76,
  //   0,75,0,ad,76,0,75,0,ac,76,0,75,0,ab,76,0,75,0,aa,76,0,75,0,a9,76,0,75,0,a8,76,0,75,
  //   0,a7,76,0,75,0,a6,76,0,75,0,a5,76,0,75,0,a4,76,0,75,0,a3,76,0,75,0,a2,76,0,75,0,a1,
  //   76,0,75,0,a0,76,0,75,0,9f,76,0,75,0,9e,76,0,75,0,9d,76,0,75,0,9c,76,0,75,0,9b,76,
  //   0,75,0,9a,76,0,75,0,99,76,0,75,0,98,76,0,75,0,97,76,0,75,0,96,76,0,75,0,95,76,0,75,
  //   0,94,76,0,75,0,93,76,0,75,0,92,76,0,75,0,91,76,0,75,0,90,76,0,75,0,8f,76,0,75,0,8e,
  //   76,0,75,0,8d,76,0,75,0,8c,76,0,75,0,8b,76,0,75,0,8a,76,0,75,0,89,76,0,75,0,88,76,
  //   0,75,0,87,76,0,75,0,86,76,0,75,0,85,76,0,75,0,84,76,0,75,0,83,76,0,75,0,82,76,0,75,
  //   0,81,76,0,75,0,80,76,0,75,0,7f,76,0,75,0,7e,76,0,75,0,7d,76,0,75,0,7c,76,0,75,0,7b,
  //   76,0,75,0,7a,76,0,75,0,79,76,0,75,0,78,76,0,75,0,77,76,0,75,0,76,76,0,75,0,75,76,
  //   0,75,0,74,76,0,75,0,73,76,0,75,0,72,76,0,75,0,71,76,0,75,0,70,76,0,75,0,6f,76,0,75,
  //   0,6e,76,0,75,0,6d,76,0,75,0,6c,76,0,75,0,6b,76,0,75,0,6a,76,0,75,0,69,76,0,75,0,68,
  //   76,0,75,0,67,76,0,75,0,66,76,0,75,0,65,76,0,75,0,64,76,0,75,0,63,76,0,75,0,62,76,
  //   0,75,0,61,76,0,75,0,60,76,0,75,0,5f,76,0,75,0,5e,76,0,75,0,5d,76,0,75,0,5c,76,0,75,
  //   0,5b,76,0,75,0,5a,76,0,75,0,59,76,0,75,0,58,76,0,75,0,57,76,0,75,0,56,76,0,75,0,55,
  //   76,0,75,0,54,76,0,75,0,53,76,0,75,0,52,76,0,75,0,51,76,0,75,0,50,76,0,75,0,4f,76,
  //   0,75,0,4e,76,0,75,0,4d,76,0,75,0,4c,76,0,75,0,4b,76,0,75,0,4a,76,0,75,0,49,76,0,75,
  //   0,48,76,0,75,0,47,76,0,75,0,46,76,0,75,0,45,76,0,75,0,44,76,0,75,0,43,76,0,75,0,42,
  //   76,0,75,0,41,76,0,75,0,40,76,0,75,0,3f,76,0,75,0,3e,76,0,75,0,3d,76,0,75,0,3c,76,
  //   0,75,0,3b,76,0,75,0,3a,76,0,75,0,39,76,0,75,0,38,76,0,75,0,37,76,0,75,0,36,76,0,75,
  //   0,35,76,0,75,0,34,76,0,75,0,33,76,0,75,0,32,76,0,75,0,31,76,0,75,0,30,76,0,75,0,2f,
  //   76,0,75,0,2e,76,0,75,0,2d,76,0,75,0,2c,76,0,75,0,2b,76,0,75,0,2a,76,0,75,0,29,76,
  //   0,75,0,28,76,0,75,0,27,76,0,75,0,26,76,0,75,0,25,76,0,75,0,24,76,0,75,0,23,76,0,75,
  //   0,22,76,0,75,0,21,76,0,75,0,20,76,0,75,0,1f,76,0,75,0,1e,76,0,75,0,1d,76,0,75,0,1c,
  //   76,0,75,0,1b,76,0,75,0,1a,76,0,75,0,19,76,0,75,0,18,76,0,75,0,17,76,0,75,0,16,76,
  //   0,75,0,15,76,0,75,0,14,76,0,75,0,13,76,0,75,0,12,76,0,75,0,11,76,0,75,0,10,76,0,75,
  //   0,f,76,0,75,0,e,76,0,75,0,d,76,0,75,0,c,76,0,75,0,b,76,0,75,0,a,76,0,75,0,9,76,0,
  //   75,0,8,76,0,75,0,7,76,0,75,0,6,76,0,75,0,5,76,0,75,0,4,76,0,75,0,3,76,0,75,0,2,76,
  //   0,75,0,1,76,0,75,0,0,76,0,75,81,0,75,82,0,75,83,0,75,d0,0,75,e0,0,75,f0,0,75,d0,0,
  //   75,0,0,76,e4,75,d0,0,75,0,1,76,b6,75,d0,0,75,0,2,76,cf,75,d0,0,75,0,3,76,aa,75,d0,
  //   0,75,0,4,76,76,75,d0,0,75,0,5,76,65,75,d0,0,75,0,6,76,7,75,d0,0,75,0,7,76,1d,75,d0,
  //   0,75,0,8,76,9e,75,d0,0,75,0,9,76,33,75,d0,0,75,0,a,76,e0,75,d0,0,75,0,b,76,a,75,d0,
  //   0,75,0,c,76,55,75,d0,0,75,0,d,76,aa,75,d0,0,75,0,e,76,3b,75,d0,0,75,0,f,76,57,75,
  //   d0,0,75,0,10,76,a4,75,d0,0,75,0,11,76,47,75,d0,0,75,0,12,76,8c,75,d0,0,75,0,13,76,
  //   b,75,d0,0,75,0,14,76,d8,75,d0,0,75,0,15,76,64,75,d0,0,75,0,16,76,bb,75,d0,0,75,0,
  //   17,76,b6,75,d0,0,75,0,18,76,f1,75,d0,0,75,0,19,76,2,75,d0,0,75,0,1a,76,80,75,d0,0,
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endmodule
