// Digital circuit STALL.dig as structural Verilog
// stop ouput clock if input S  is high. if go is 1, clock will ouput normally.
module STALL (
  input  C,
  input  AC,
  input  S,
  input  G,
  input  nCLR,
  output O,
  output OAC
);

  wire and_1_out, and_3_out, INTR_q, not_1_out, not_2_out, not_3_out, or_1_out, or_2_out, register_1_q,
       SYNC0_q, SYNC1_q;

  not not_1 (not_1_out, C);
  Register SYNC0 (.D(G), .C(not_1_out), .en(1'b1), .Q(SYNC0_q));
  Register SYNC1 (.D(SYNC0_q), .C(not_1_out), .en(1'b1), .Q(SYNC1_q));
  Register register_1 (.D(SYNC1_q), .C(not_1_out), .en(1'b1), .Q(register_1_q));
  not not_2 (not_2_out, SYNC1_q);
  or or_1 (or_1_out, INTR_q, S);
  or or_2 (or_2_out, register_1_q, not_2_out);
  and and_1 (and_1_out, or_1_out, nCLR, or_2_out);
  Register INTR (.D(and_1_out), .C(not_1_out), .en(1'b1), .Q(INTR_q));
  not not_3 (not_3_out, INTR_q);
  and and_2 (OAC, AC, not_3_out);
  and and_3 (and_3_out, C, not_3_out);
  Delay delay_1 (.in(and_3_out), .out(O));

  // Notes on the sheet:
  //   O: clock output
  //   S: stop clock
  //   G: continue clock. enable CLKO when detected raise edge. sync with ~CLKI
  //   OAC: clock output
  //   nCLR: stop clock
endmodule
