// Digital circuit XRAM.dig as structural Verilog
// stop ouput clock if input S  is high. if go is 1, clock will ouput normally.
module XRAM (
  input  CLKA,
  input  [15:0] A,
  input  WE,
  input  nOE,
  output [7:0] O
);

  // NAnd nand_1 has open pins: In_1=WE, In_2=CLKA, out=open

  // Notes on the sheet:
  //   CLKA: Asynchronous clock specially prepared for RAM
  //   A: address
endmodule
