// Digital circuit reg-file.dig as structural Verilog
module reg_file (
  input  CLK,
  input  [3:0] RS,
  input  [7:0] D,
  input  LLE,
  input  HLE,
  output [7:0] Q
);

  RAMDualPort #(.AddrBits(4), .Bits(4)) RFL (.A(RS), .Din(D[3:0]), .str(LLE), .C(CLK), .ld(1'b1), .D(Q[3:0]));
  RAMDualPort #(.AddrBits(4), .Bits(4)) RFH (.A(RS), .Din(D[7:4]), .str(HLE), .C(CLK), .ld(1'b1), .D(Q[7:4]));
endmodule
